# Fritzing sketch ServoAutomat (saved by Fritzing 0.9.4)
circuit board: 9.90173cm x 7.2782cm
breadboards: 1

parts:
  Bauteil1 = Arduino Nano (Rev3.0)
  LED1 = LED - 5mm [color="Green (565nm)" package="5 mm [THT]"]
  R1 = Resistor [tolerance=±5% resistance=680 package=THT]
  S1 = Pushbutton [package="[THT]"]
  J1 = female pin header, 3 pins [form="♀ (female)"]
  J2 = Screw terminal - 2 pins [package=THT]
  C1 = Ceramic Capacitor [capacitance=100nF package="100 mil [THT, multilayer]"]
  C2 = Electrolytic Capacitor [capacitance=470µF voltage=16V package="100 mil [THT, electrolytic]"]
  J3 = Screw terminal - 2 pins [package=THT]

nets:
  N1: Bauteil1.GND, Bauteil1.D5, S1.Pin_1, S1.Pin_2, S1.Pin_3, S1.Pin_4, J1.pin1, J2.pin2, C1.0, C2.-, J3.pin2
  N2: Bauteil1.D4, J1.pin3
  N3: Bauteil1.D10, LED1.cathode
  N4: Bauteil1.5V, R1.Pin_1, J3.pin1
  N5: LED1.anode, R1.Pin_0
  N6: J1.pin2, J2.pin1, C1.1, C2.+
